# Fritzing sketch Scanduino Fritzing diagram (saved by Fritzing 0.7.11b)
breadboards: 1

parts:
  Arduino1 = Arduino
  U1 = Optocoupler [package=THT]
  U2 = Optocoupler [package=THT]
  M1 = Stepper Motor - Bipolar
  S1 = Pushbutton [package="[THT]"]
  Part1 = EasyDriver_v44
  R7 = Resistor [tolerance=±5% resistance=330 package=THT]
  R8 = Resistor [tolerance=±5% resistance=330 package=THT]
  Part2 = DeuLigne 1.1 - The Snootlab's LCD shield for Arduino
  S5 = Pushbutton [package="[THT]"]
  S6 = Pushbutton [package="[THT]"]
  S7 = Pushbutton [package="[THT]"]
  S8 = Pushbutton [package="[THT]"]
  Part3 = EasyDriver_v44
  M2 = Stepper Motor - Bipolar
  Part4 = Thumb Joystick
  TRS1 = Audio Jack (TRS) 3.5mm [package="PG203J [THT]"]

nets:
  N1: Arduino1.D11, R8.Pin_1
  N2: Arduino1.D10, R7.Pin_1
  N3: Arduino1.D9, S7.Pin_3
  N4: Arduino1.D8, S6.Pin_1
  N5: Arduino1.D7, Part3.STEP
  N6: Arduino1.D6, Part3.DIR
  N7: Arduino1.D5, Part1.STEP
  N8: Arduino1.D4, Part1.DIR
  N9: Arduino1.D3, Part4.SEL
  N10: Arduino1.D2, S1.Pin_3, S1.Pin_4
  +5V: Arduino1.+5V, Part2.+5V, Part4.VCC
  GND: Arduino1.GND, U1.Pin_2, U1.Pin_4, U2.Pin_2, U2.Pin_4, S1.Pin_1, S1.Pin_2, Part1.GND, Part2.GND, S5.Pin_1, S5.Pin_2, S6.Pin_4, S7.Pin_2, S8.Pin_4, Part3.GND, Part4.GND, TRS1.Sleeve
  N11: Arduino1.A2, Part4.HORZ
  N12: Arduino1.A3, Part4.VERT
  N13: Arduino1.A4, Part2.A4(SDA)
  N14: Arduino1.A5, Part2.A5(CLK)
  N15: U1.Pin_1, R7.Pin_0
  N16: U1.Pin_5, TRS1.Ring
  N17: U2.Pin_1, R8.Pin_0
  N18: U2.Pin_5, TRS1.Tip
  N19: M1.A, Part1.OUT2A
  N20: M1.C, Part1.OUT2B
  N21: M1.B, Part1.OUT1A
  N22: M1.D, Part1.OUT1B
  N23: Part1.V+, Part3.V+
  N24: Part3.OUT2A, M2.A
  N25: Part3.OUT2B, M2.C
  N26: Part3.OUT1A, M2.B
  N27: Part3.OUT1B, M2.D

notes:
  limit SW X
  limit SW Y
  7-30V DC Power to Easydrivers
  3.5mm jack to camera
  SCANDUINO
  by Really Small
  Tie Easydriver MS1 and MS2 to ground to enable whole stepping
